# Fritzing sketch Servo (saved by Fritzing 0.9.3b)
breadboards: 1

parts:
  WeMos_D1_Mini1 = WeMos D1 Mini
  V1 = DC Power [voltage=5]
  S1 = Round Pushbutton
  R1 = Resistor [tolerance=±5% resistance=1k package="0805 [SMD]"]
  R2 = Resistor [tolerance=±5% resistance=1k package="0805 [SMD]"]
  R3 = Resistor [tolerance=±5% resistance=1k package="0805 [SMD]"]
  R4 = Resistor [tolerance=±5% resistance=1k package="0805 [SMD]"]
  S2 = Round Pushbutton
  S3 = Reed switch [package=THT]
  S4 = Toggle Switch [package=THT]
  S5 = Toggle Switch [package=THT]
  R5 = Resistor [tolerance=±5% resistance=1k package="0805 [SMD]"]
  J1 = Basic Servo
  WeMos_D1_Mini_Relay_Shield_V1 = WeMos D1 Mini Relay Shield V2

nets:
  5V: WeMos_D1_Mini1.5V, V1.V+, R1.Pin_1, R2.Pin_1, R3.Pin_1, R4.Pin_1, R5.Pin_0, J1.vcc, WeMos_D1_Mini_Relay_Shield_V1.5V
  N1: WeMos_D1_Mini1.D1, WeMos_D1_Mini_Relay_Shield_V1.D1
  N2: WeMos_D1_Mini1.D2, S3.pin_2, R5.Pin_1
  N3: WeMos_D1_Mini1.D4, J1.pulse
  N4: WeMos_D1_Mini1.D5, R1.Pin_0
  N5: WeMos_D1_Mini1.D6, R2.Pin_0
  N6: WeMos_D1_Mini1.D7, R3.Pin_0
  N7: WeMos_D1_Mini1.D8, R4.Pin_0
  N8: WeMos_D1_Mini1.G, V1.V-, S1.leg0, S2.leg0, S3.pin_1, S4.COM, S5.COM, J1.gnd, WeMos_D1_Mini_Relay_Shield_V1.G
